// Logisim project PIC8.circ as structural Verilog: 25 circuits, main circuit main
module main (
  input  reset,
  input  [7:0] in_2
);

  wire CLK, not_1_out, regbank_1_write_ram, RES_SEL, uc_1_data_write, uc_1_jump, uc_1_op, uc_1_pc_enable,
       uc_1_skip;
  wire [1:0] uc_1_literal_sel;
  wire [5:0] ADDR_IN, ADDR_OUT, ADDR_OUT2;
  wire [7:0] DATA, multiplexer_1_out, multiplexer_2_out, multiplexer_3_out, pc_1_rom_addr, PORTA,
       regbank_1_data_out, regbank_1_data_out2, regbank_1_endereco_ram, regbank_1_input_ram,
       regbank_1_work_out, RES, uc_1_goto, uc_1_literal_data;
  wire [12:0] rom_1_data;

  ROM #(.dataWidth(13)) rom_1 (.addr(pc_1_rom_addr), .data(rom_1_data));
  PC pc_1 (
    .reset(reset), .enable(uc_1_pc_enable), .clock(CLK), .addr_in(uc_1_goto), .jump(uc_1_jump),
    .skip(uc_1_skip), .rom_addr(pc_1_rom_addr));
  Multiplexer #(.width(8), .enable("false")) multiplexer_1 (
    .in0(DATA), .in1(RES), .out(multiplexer_1_out), .sel(RES_SEL));
  // Probe on multiplexer_1_out
  UC uc_1 (
    .clock(CLK), .reset(reset), .opcode(rom_1_data), .data_out(regbank_1_data_out),
    .data_out2(regbank_1_data_out2), .work(regbank_1_work_out), .literal_data(uc_1_literal_data),
    .literal_sel(uc_1_literal_sel), .res_sel(RES_SEL), .op(uc_1_op), .data(DATA),
    .data_write(uc_1_data_write), .addr_in(ADDR_IN), .addr_out(ADDR_OUT), .goto(uc_1_goto), .jump(uc_1_jump),
    .pc_enable(uc_1_pc_enable), .skip(uc_1_skip), .addr_out2(ADDR_OUT2));
  // Probe on regbank_1_work_out
  regBank regbank_1 (
    .data_in(multiplexer_1_out), .write_data(uc_1_data_write), .endereco_in(ADDR_IN),
    .endereco_out(ADDR_OUT), .clock(CLK), .reset(reset), .output_ram(multiplexer_3_out),
    .endereco_out2(ADDR_OUT2), .data_out(regbank_1_data_out), .write_ram(regbank_1_write_ram),
    .input_ram(regbank_1_input_ram), .endereco_ram(regbank_1_endereco_ram), .port_a(PORTA), .port_b(in_2),
    .work_out(regbank_1_work_out), .data_out2(regbank_1_data_out2));
  Multiplexer #(.select(2), .width(8), .enable("false")) multiplexer_2 (
    .in0(regbank_1_work_out), .in1(regbank_1_data_out), .in2(uc_1_literal_data), .in3(regbank_1_data_out2),
    .out(multiplexer_2_out), .sel(uc_1_literal_sel));
  Clock clock_1 (.out(CLK));
  // Probe on RES_SEL
  // Probe on ADDR_IN
  Multiplexer #(.width(8), .enable("false")) multiplexer_3 (
    .in1(regbank_1_input_ram), .out(multiplexer_3_out), .sel(regbank_1_write_ram));  // open: in0
  RAM ram_1 (
    .addr(regbank_1_endereco_ram), .we(regbank_1_write_ram), .oe(not_1_out), .clk(CLK),
    .data(multiplexer_3_out));
  not not_1 (not_1_out, regbank_1_write_ram);
  ULA ula_1 (
    .input_A(regbank_1_data_out), .input_B(multiplexer_2_out), .Op(uc_1_op), .result(RES));  // open: zero, carry

  // Other names for the same wires on the sheet: PORTB[7:0] = in_2; RST = reset

  // Notes on the sheet:
  //   contents of rom_1 (hex, n*v repeats v):
  //   1801 41 fe 541 401 7e 1e1f 46 fc6 1403 1802 41 fe 541 541 1820 101 46 dc6 140c 1806 41 fe 541 541
  //   541 1820 101 46 dc6 1416 1810 41 fe 1805 3c1 1820 101 46 dc6 1421 1800 41 541 1801 13e 47 fc7 1437
  //   1820 101 46 dc6 142b 1429 43e 45 142b 20*0 1000 0 31 31 30 a 31 31 31 1100 0 30 30 31 30 30 0 0 30 a
  //   30 31 31 31 30 31 30 4*31 30 0 0 31 30 31 30 30
endmodule

module reg8bits (
  input  [7:0] data_in,
  input  enable,
  input  clock,
  input  reset,
  output [7:0] data_out
);

  wire and_1_out, and_2_out, and_3_out, and_4_out, and_5_out, and_6_out, and_7_out, and_8_out;

  and and_1 (and_1_out, enable, clock);
  and and_2 (and_2_out, enable, clock);
  and and_3 (and_3_out, enable, clock);
  and and_4 (and_4_out, enable, clock);
  and and_5 (and_5_out, enable, clock);
  and and_6 (and_6_out, enable, clock);
  and and_7 (and_7_out, enable, clock);
  and and_8 (and_8_out, enable, clock);
  D_Flip_Flop d_ff_1 (.D(data_in[0]), .clk(and_1_out), .Q(data_out[0]), .reset(reset));  // open: Qn, preset
  D_Flip_Flop d_ff_2 (.D(data_in[1]), .clk(and_2_out), .Q(data_out[1]), .reset(reset));  // open: Qn, preset
  D_Flip_Flop d_ff_3 (.D(data_in[2]), .clk(and_3_out), .Q(data_out[2]), .reset(reset));  // open: Qn, preset
  D_Flip_Flop d_ff_4 (.D(data_in[3]), .clk(and_4_out), .Q(data_out[3]), .reset(reset));  // open: Qn, preset
  D_Flip_Flop d_ff_5 (.D(data_in[4]), .clk(and_5_out), .Q(data_out[4]), .reset(reset));  // open: Qn, preset
  D_Flip_Flop d_ff_6 (.D(data_in[5]), .clk(and_6_out), .Q(data_out[5]), .reset(reset));  // open: Qn, preset
  D_Flip_Flop d_ff_7 (.D(data_in[6]), .clk(and_7_out), .Q(data_out[6]), .reset(reset));  // open: Qn, preset
  D_Flip_Flop d_ff_8 (.D(data_in[7]), .clk(and_8_out), .Q(data_out[7]), .reset(reset));  // open: Qn, preset

  // Other names for the same wires on the sheet: CLK = clock; D0 = data_in[0]; D1 = data_in[1]; D2 = data_in[2];
  //   D3 = data_in[3]; D4 = data_in[4]; D5 = data_in[5]; D6 = data_in[6]; D7 = data_in[7]; ENB = enable; RST = reset
endmodule

module regBank (
  input  [7:0] data_in,
  input  write_data,
  input  [5:0] endereco_in,
  input  [5:0] endereco_out,
  input  clock,
  input  reset,
  input  [7:0] output_ram,
  input  [5:0] endereco_out2,
  output [7:0] data_out,
  output write_ram,
  output [7:0] input_ram,
  output [7:0] endereco_ram,
  output [7:0] port_a,
  output [7:0] port_b,
  output [7:0] work_out,
  output [7:0] data_out2
);

  wire demultiplexer_1_out0, demultiplexer_1_out1, fsr, portA, portB, s1, s2, s3, s4, s5, s6, s7, s8, s9,
       s10, s11, s12, s13, s14, s15, s16, status, trisA, trisB, work;
  wire [7:0] multiplexer_1_out, multiplexer_2_out, multiplexer_4_out, multiplexer_5_out, outS1, outS2, outS3,
       outS4, outS5, outS6, outS7, outS8, outS9, outS10, outS11, outS12, outS13, outS14, outS15, outS16,
       outStatus, outTrisA, outTrisB;

  Demultiplexer #(.enable("false")) demultiplexer_1 (
    .out0(demultiplexer_1_out0), .out1(demultiplexer_1_out1), .in(write_data), .sel(endereco_in[5]));
  Demultiplexer #(.select(5), .enable("false")) demultiplexer_2 (
    .out1(fsr), .out2(trisA), .out3(trisB), .out4(portA), .out5(portB), .out6(s1), .out7(s2), .out8(s3),
    .out9(s4), .out10(s5), .out11(s6), .out12(s7), .out13(s8), .out14(s9), .out15(s10), .out16(s11),
    .out17(s12), .out18(s13), .out19(s14), .out20(s15), .out21(s16), .in(demultiplexer_1_out0),
    .sel(endereco_in[4:0]));  // open: out0, out22, out23, out24, out25, out26, out27, out28, out29, out30, out31
  Demultiplexer #(.select(5), .enable("false")) demultiplexer_3 (
    .out29(status), .out30(write_ram), .out31(work), .in(demultiplexer_1_out1), .sel(endereco_in[4:0]));  // open: out0, out1, out2, out3, out4, out5, out6, out7, out8, out9, out10, out11, out12, out13, out14, out15, out16, out17, out18, out19, out20, out21, out22, out23, out24, out25, out26, out27, out28
  reg8bits u_FSR (.data_in(data_in), .enable(fsr), .clock(clock), .reset(reset), .data_out(endereco_ram));
  // Probe on endereco_ram
  reg8bits u_TRISA (.data_in(data_in), .enable(trisA), .clock(clock), .reset(reset), .data_out(outTrisA));
  // Probe on outTrisA
  reg8bits u_TRISB (.data_in(data_in), .enable(trisB), .clock(clock), .reset(reset), .data_out(outTrisB));
  // Probe on outTrisB
  reg8bits u_PORTA (.data_in(data_in), .enable(portA), .clock(clock), .reset(reset), .data_out(port_a));
  // Probe on port_a
  reg8bits u_PORTB (.data_in(data_in), .enable(portB), .clock(clock), .reset(reset), .data_out(port_b));
  // Probe on port_b
  reg8bits u_STATUS (.data_in(data_in), .enable(status), .clock(clock), .reset(reset), .data_out(outStatus));
  // Probe on outStatus
  reg8bits u_WORK (.data_in(data_in), .enable(work), .clock(clock), .reset(reset), .data_out(work_out));
  // Probe on work_out
  Multiplexer #(.select(5), .width(8), .enable("false")) multiplexer_1 (
    .in0({8{1'b0}}), .in1(endereco_ram), .in2(outTrisA), .in3(outTrisB), .in4(port_a), .in5(port_b),
    .in6(outS1), .in7(outS2), .in8(outS3), .in9(outS4), .in10(outS5), .in11(outS6), .in12(outS7),
    .in13(outS8), .in14(outS9), .in15(outS10), .in16(outS11), .in17(outS12), .in18(outS13), .in19(outS14),
    .in20(outS15), .in21(outS16), .out(multiplexer_1_out), .sel(endereco_out2[4:0]));  // open: in22, in23, in24, in25, in26, in27, in28, in29, in30, in31
  Multiplexer #(.select(5), .width(8), .enable("false")) multiplexer_2 (
    .in29(outStatus), .in30(output_ram), .in31(work_out), .out(multiplexer_2_out), .sel(endereco_out2[4:0]));  // open: in0, in1, in2, in3, in4, in5, in6, in7, in8, in9, in10, in11, in12, in13, in14, in15, in16, in17, in18, in19, in20, in21, in22, in23, in24, in25, in26, in27, in28
  reg8bits u_S1 (.data_in(data_in), .enable(s1), .clock(clock), .reset(reset), .data_out(outS1));
  // Probe on outS1
  reg8bits u_S2 (.data_in(data_in), .enable(s2), .clock(clock), .reset(reset), .data_out(outS2));
  // Probe on outS2
  reg8bits u_S3 (.data_in(data_in), .enable(s3), .clock(clock), .reset(reset), .data_out(outS3));
  // Probe on outS3
  reg8bits u_S4 (.data_in(data_in), .enable(s4), .clock(clock), .reset(reset), .data_out(outS4));
  // Probe on outS4
  reg8bits u_S5 (.data_in(data_in), .enable(s5), .clock(clock), .reset(reset), .data_out(outS5));
  // Probe on outS5
  reg8bits u_S6 (.data_in(data_in), .enable(s6), .clock(clock), .reset(reset), .data_out(outS6));
  // Probe on outS6
  reg8bits u_S7 (.data_in(data_in), .enable(s7), .clock(clock), .reset(reset), .data_out(outS7));
  // Probe on outS7
  Multiplexer #(.width(8), .enable("false")) multiplexer_3 (
    .in0(multiplexer_1_out), .in1(multiplexer_2_out), .out(data_out2), .sel(endereco_out2[5]));
  Multiplexer #(.select(5), .width(8), .enable("false")) multiplexer_4 (
    .in0({8{1'b0}}), .in1(endereco_ram), .in2(outTrisA), .in3(outTrisB), .in4(port_a), .in5(port_b),
    .in6(outS1), .in7(outS2), .in8(outS3), .in9(outS4), .in10(outS5), .in11(outS6), .in12(outS7),
    .in13(outS8), .in14(outS9), .in15(outS10), .in16(outS11), .in17(outS12), .in18(outS13), .in19(outS14),
    .in20(outS15), .in21(outS16), .out(multiplexer_4_out), .sel(endereco_out[4:0]));  // open: in22, in23, in24, in25, in26, in27, in28, in29, in30, in31
  Multiplexer #(.select(5), .width(8), .enable("false")) multiplexer_5 (
    .in29(outStatus), .in30(output_ram), .in31(work_out), .out(multiplexer_5_out), .sel(endereco_out[4:0]));  // open: in0, in1, in2, in3, in4, in5, in6, in7, in8, in9, in10, in11, in12, in13, in14, in15, in16, in17, in18, in19, in20, in21, in22, in23, in24, in25, in26, in27, in28
  reg8bits u_S8 (.data_in(data_in), .enable(s8), .clock(clock), .reset(reset), .data_out(outS8));
  reg8bits u_S9 (.data_in(data_in), .enable(s9), .clock(clock), .reset(reset), .data_out(outS9));
  reg8bits u_S10 (.data_in(data_in), .enable(s10), .clock(clock), .reset(reset), .data_out(outS10));
  reg8bits u_S11 (.data_in(data_in), .enable(s11), .clock(clock), .reset(reset), .data_out(outS11));
  reg8bits u_S12 (.data_in(data_in), .enable(s12), .clock(clock), .reset(reset), .data_out(outS12));
  reg8bits u_S13 (.data_in(data_in), .enable(s13), .clock(clock), .reset(reset), .data_out(outS13));
  reg8bits u_S14 (.data_in(data_in), .enable(s14), .clock(clock), .reset(reset), .data_out(outS14));
  Multiplexer #(.width(8), .enable("false")) multiplexer_6 (
    .in0(multiplexer_4_out), .in1(multiplexer_5_out), .out(data_out), .sel(endereco_out[5]));
  // Probe on outS8
  // Probe on outS9
  // Probe on outS10
  // Probe on outS11
  // Probe on outS12
  // Probe on outS13
  // Probe on outS14
  reg8bits u_S15 (.data_in(data_in), .enable(s15), .clock(clock), .reset(reset), .data_out(outS15));
  // Probe on outS15
  reg8bits u_S16 (.data_in(data_in), .enable(s16), .clock(clock), .reset(reset), .data_out(outS16));
  // Probe on outS16

  assign input_ram = data_in;

  // Other names for the same wires on the sheet: clk = clock; dt[7:0] = data_in; indf = write_ram;
  //   outFsr[7:0] = endereco_ram; outPortA[7:0] = port_a; outPortB[7:0] = port_b; outWork[7:0] = work_out;
  //   RAM[7:0] = output_ram; rst = reset
endmodule

module reg8bits_test (
  input  in_1
);

  wire clock_1_out;
  wire [7:0] counter_1_q, reg8bits_1_data_out;

  Counter counter_1 (.clr(in_1), .up(1'b1), .clk(clock_1_out), .Q(counter_1_q));  // open: load, count, D, carry
  Clock clock_1 (.out(clock_1_out));
  // Probe on counter_1_q
  reg8bits reg8bits_1 (
    .data_in(counter_1_q), .enable(1'b1), .clock(clock_1_out), .data_out(reg8bits_1_data_out));  // open: reset
  // Probe on reg8bits_1_data_out
endmodule

module regBank_test (
  input  in_1,
  input  in_2
);

  wire clock_1_out, or_1_out, regbank_1_p6;
  wire [5:0] counter_1_q;
  wire [7:6] counter_1_q_2;

  or or_1 (or_1_out, counter_1_q_2[6], in_2);
  Clock clock_1 (.out(clock_1_out));
  Counter counter_1 (
    .clr(or_1_out), .up(1'b1), .clk(clock_1_out), .Q({counter_1_q_2, counter_1_q}));  // open: load, count, D, carry
  // Probe on {counter_1_q_2, counter_1_q}
  // Probe on counter_1_q
  // regBank regbank_1: pin names not known; wires that end beside it: in_1, counter_1_q, counter_1_q, clock_1_out, {counter_1_q_2, counter_1_q}, regbank_1_p6
  // Probe on regbank_1_p6
endmodule

module ram_test (
  input  [5:0] in_1,
  input  [5:0] in_2,
  input  in_3,
  input  in_4,
  input  [5:0] in_5
);

  wire clock_1_out, demultiplexer_1_out0, demultiplexer_1_out1, multiplexer_2_out, not_1_out, not_2_out,
       or_1_out, regbank_1_p7, regbank_1_p8;
  wire [7:0] counter_1_q, regbank_1_p6, regbank_1_p9, regbank_1_p10;

  Clock clock_1 (.out(clock_1_out));
  or or_1 (or_1_out, counter_1_q[5], in_4);
  Counter counter_1 (
    .clr(or_1_out), .up(counter_1_q[0]), .clk(clock_1_out), .Q(counter_1_q));  // open: load, count, D, carry
  Multiplexer #(.width(6), .enable("false")) multiplexer_1 (
    .in0(in_1), .in1(in_2), .out(counter_1_q[5:0]), .sel(multiplexer_2_out));
  Multiplexer #(.enable("false")) multiplexer_2 (
    .in0(not_1_out), .in1(demultiplexer_1_out1), .out(multiplexer_2_out), .sel(in_3));
  not not_1 (not_1_out, demultiplexer_1_out0);
  Demultiplexer #(.enable("false")) demultiplexer_1 (
    .out0(demultiplexer_1_out0), .out1(demultiplexer_1_out1), .in(counter_1_q[0]), .sel(in_3));
  // regBank regbank_1: pin names not known; wires that end beside it: counter_1_q, counter_1_q, counter_1_q, in_5, clock_1_out, regbank_1_p6, regbank_1_p7, regbank_1_p8, regbank_1_p9, regbank_1_p10
  // Probe on regbank_1_p7
  Multiplexer #(.width(8), .enable("false")) multiplexer_3 (
    .in1(regbank_1_p9), .out(regbank_1_p6), .sel(regbank_1_p8));  // open: in0
  RAM ram_1 (.addr(regbank_1_p10), .we(regbank_1_p8), .oe(not_2_out), .clk(clock_1_out), .data(regbank_1_p6));
  not not_2 (not_2_out, regbank_1_p8);
  // Probe on regbank_1_p6
  // Pins of 1 and 6 and 8 bits meet at counter_1_q
  // also tied to VCC on the sheet: counter_1_q[0]
endmodule

module ULA (
  input  [7:0] input_A,
  input  [7:0] input_B,
  input  Op,
  output zero,
  output carry,
  output [7:0] result
);

  wire adder_1_cout, subtractor_2_bout;
  wire [7:0] adder_1_out, demultiplexer_1_out0, demultiplexer_1_out1, demultiplexer_2_out0,
       demultiplexer_2_out1, subtractor_1_out, subtractor_2_out;

  Demultiplexer #(.width(8), .enable("false")) demultiplexer_1 (
    .out0(demultiplexer_1_out0), .out1(demultiplexer_1_out1), .in(input_A), .sel(Op));
  Demultiplexer #(.width(8), .enable("false")) demultiplexer_2 (
    .out0(demultiplexer_2_out0), .out1(demultiplexer_2_out1), .in(input_B), .sel(Op));
  Subtractor subtractor_1 (.a(input_A), .b(input_B), .out(subtractor_1_out));  // open: bin, bout
  Adder adder_1 (
    .a(demultiplexer_1_out0), .b(demultiplexer_2_out0), .out(adder_1_out), .cout(adder_1_cout));  // open: cin
  Subtractor subtractor_2 (
    .a(demultiplexer_2_out1), .b(demultiplexer_1_out1), .out(subtractor_2_out), .bout(subtractor_2_bout));  // open: bin
  and and_1 (zero, ~subtractor_1_out[0], ~subtractor_1_out[1], ~subtractor_1_out[2], ~subtractor_1_out[3], ~subtractor_1_out[4], ~subtractor_1_out[5], ~subtractor_1_out[6], ~subtractor_1_out[7]);  // AND_Gate
  or or_1 (carry, adder_1_cout, subtractor_2_bout);
  Multiplexer #(.width(8), .enable("false")) multiplexer_1 (
    .in0(adder_1_out), .in1(subtractor_2_out), .out(result), .sel(Op));
endmodule

module UC (
  input  clock,
  input  reset,
  input  [12:0] opcode,
  input  [7:0] data_out,
  input  [7:0] data_out2,
  input  [7:0] work,
  output [7:0] literal_data,
  output [1:0] literal_sel,
  output res_sel,
  output op,
  output [7:0] data,
  output data_write,
  output [5:0] addr_in,
  output [5:0] addr_out,
  output [7:0] goto,
  output jump,
  output pc_enable,
  output skip,
  output [5:0] addr_out2
);

  wire P1, P2, P3, P4, P5, P6, P7, P8, P9, P10, P11, seletor_1_data_wr, seletor_1_jump, seletor_1_op,
       seletor_1_pc_enable, seletor_1_res_sel, seletor_1_skip;
  wire [1:0] seletor_1_literal_sel;
  wire [4:0] decode_1_sel;
  wire [5:0] ADDR_OUT2_t, seletor_1_addr_in, seletor_1_addr_out;
  wire [7:0] seletor_1_data, seletor_1_goto, seletor_1_literal_data;
  wire [11:0] B1, B2, B3, B4, B5, B6, B7, B8, B9, B10, B11;
  wire [31:0] A1, A2, A3, A4, A5, A6, A7, A8, A9, A10, A11;

  fun_movlw fun_movlw_1 (.opcode(opcode), .active(P1), .a(A1), .b(B1));
  fun_movwf fun_movwf_1 (.opcode(opcode), .data_out(work), .active(P2), .a(A2), .b(B2));
  fun_movf fun_movf_1 (.opcode(opcode), .active(P3), .a(A3), .b(B3));
  fun_clrf fun_clrf_1 (.opcode(opcode), .active(P4), .a(A4), .b(B4));
  fun_sublw fun_sublw_1 (.opcode(opcode), .active(P5), .a(A5), .b(B5));
  fun_incf fun_incf_1 (.opcode(opcode), .active(P6), .a(A6), .b(B6));
  fun_btfss fun_btfss_1 (.opcode(opcode), .data_out(data_out), .active(P7), .a(A7), .b(B7));
  fun_goto fun_goto_1 (.opcode(opcode), .active(P8), .a(A8), .b(B8));
  fun_btfsc fun_btfsc_1 (.opcode(opcode), .data_out(data_out), .active(P10), .a(A10), .b(B10));
  fun_subwf fun_subwf_1 (.opcode(opcode), .active(P9), .a(A9), .b(B9), .addr_out2(ADDR_OUT2_t));
  decode decode_1 (
    .p1(P1), .p2(P2), .p3(P3), .p4(P4), .p5(P5), .p6(P6), .p7(P7), .p8(P8), .p9(P9), .p10(P10), .p11(P11),
    .sel(decode_1_sel));
  seletor seletor_1 (
    .sel(decode_1_sel), .a1_in(A1), .a2_in(A2), .a3_in(A3), .a4_in(A4), .a5_in(A5), .a6_in(A6), .a7_in(A7),
    .a8_in(A8), .a9_in(A9), .a10_in(A10), .a11_in(A11), .b1_in(B1), .b2_in(B2), .b3_in(B3), .b4_in(B4),
    .b5_in(B5), .b6_in(B6), .b7_in(B7), .b8_in(B8), .b9_in(B9), .b10_in(B10), .b11_in(B11),
    .literal_data(seletor_1_literal_data), .literal_sel(seletor_1_literal_sel), .res_sel(seletor_1_res_sel),
    .op(seletor_1_op), .data(seletor_1_data), .data_wr(seletor_1_data_wr), .addr_in(seletor_1_addr_in),
    .addr_out(seletor_1_addr_out), .goto(seletor_1_goto), .jump(seletor_1_jump),
    .pc_enable(seletor_1_pc_enable), .skip(seletor_1_skip));
  Register #(.trigger("falling")) register_1 (
    .D(seletor_1_literal_data), .en(1'b1), .clk(clock), .Q(literal_data), .clr(reset));
  Register #(.width(2), .trigger("falling")) register_2 (
    .D(seletor_1_literal_sel), .en(1'b1), .clk(clock), .Q(literal_sel), .clr(reset));
  Register #(.width(1), .trigger("falling")) register_3 (
    .D(seletor_1_res_sel), .en(1'b1), .clk(clock), .Q(res_sel), .clr(reset));
  Register #(.width(1), .trigger("falling")) register_4 (.D(seletor_1_op), .en(1'b1), .clk(clock), .Q(op), .clr(reset));
  Register #(.trigger("falling")) register_5 (.D(seletor_1_data), .en(1'b1), .clk(clock), .Q(data), .clr(reset));
  Register #(.width(1), .trigger("falling")) register_6 (
    .D(seletor_1_data_wr), .en(1'b1), .clk(clock), .Q(data_write), .clr(reset));
  Register #(.width(6), .trigger("falling")) register_7 (
    .D(seletor_1_addr_in), .en(1'b1), .clk(clock), .Q(addr_in), .clr(reset));
  Register #(.width(6), .trigger("falling")) register_8 (
    .D(seletor_1_addr_out), .en(1'b1), .clk(clock), .Q(addr_out), .clr(reset));
  Register #(.trigger("falling")) register_9 (.D(seletor_1_goto), .en(1'b1), .clk(clock), .Q(goto), .clr(reset));
  Register #(.width(1), .trigger("falling")) register_10 (
    .D(seletor_1_jump), .en(1'b1), .clk(clock), .Q(jump), .clr(reset));
  Register #(.width(1), .trigger("falling")) register_11 (
    .D(seletor_1_pc_enable), .en(1'b1), .clk(clock), .Q(pc_enable), .clr(reset));
  Register #(.width(1), .trigger("falling")) register_12 (
    .D(seletor_1_skip), .en(1'b1), .clk(clock), .Q(skip), .clr(reset));
  Register #(.width(6), .trigger("falling")) register_13 (
    .D(ADDR_OUT2_t), .en(1'b1), .clk(clock), .Q(addr_out2));  // open: clr

  // Other names for the same wires on the sheet: CLK = clock; res = reset
endmodule

module pc_test (
  input  in_1,
  input  in_2,
  input  [7:0] in_3,
  input  in_4,
  input  in_5
);

  wire clock_1_out;
  wire [7:0] pc_1_rom_addr;
  wire [12:0] rom_1_data;

  Clock clock_1 (.out(clock_1_out));
  PC pc_1 (
    .reset(in_1), .enable(in_2), .clock(clock_1_out), .addr_in(in_3), .jump(in_4), .skip(in_5),
    .rom_addr(pc_1_rom_addr));
  ROM #(.dataWidth(13)) rom_1 (.addr(pc_1_rom_addr), .data(rom_1_data));
  // Probe on rom_1_data

  // Notes on the sheet:
  //   contents of rom_1 (hex, n*v repeats v):
  //   1801 41 fe 541 401 7e 1e1f 46 fc6 1403 1802 41 fe 541 541 1820 101 46 dc6 140c 1803 41 fe 541 541
  //   541 1820 101 46 dc6 1416 1805 41 fe 1805 3c1 1820 101 46 dc6 1421 1800 41 541 1801 13e 47 fc7 1437
  //   1820 101 46 dc6 142b 1429 43e 45 142b 20*0 1000 0 31 31 30 a 31 31 31 1100 0 30 30 31 30 30 0 0 30 a
  //   30 31 31 31 30 31 30 4*31 30 0 0 31 30 31 30
endmodule

module PC (
  input  reset,
  input  enable,
  input  clock,
  input  [7:0] addr_in,
  input  jump,
  input  skip,
  output [7:0] rom_addr
);

  wire and_1_out, and_2_out, or_1_out, or_2_out;
  wire [7:0] adder_1_out, multiplexer_1_out;

  and and_1 (and_1_out, enable, clock);
  or or_1 (or_1_out, reset, and_2_out);
  Multiplexer #(.width(8), .enable("false")) multiplexer_1 (
    .in0(adder_1_out), .in1(addr_in), .out(multiplexer_1_out), .sel(jump));
  or or_2 (or_2_out, jump, skip);
  Counter counter_1 (
    .clr(or_1_out), .load(or_2_out), .up(1'b1), .clk(and_1_out), .D(multiplexer_1_out), .Q(rom_addr));  // open: count, carry
  and and_2 (and_2_out, rom_addr[0], rom_addr[6]);
  Adder adder_1 (.a(rom_addr), .b(8'h2), .out(adder_1_out));  // open: cin, cout
endmodule

module seletor (
  input  [4:0] sel,
  input  [31:0] a1_in,
  input  [31:0] a2_in,
  input  [31:0] a3_in,
  input  [31:0] a4_in,
  input  [31:0] a5_in,
  input  [31:0] a6_in,
  input  [31:0] a7_in,
  input  [31:0] a8_in,
  input  [31:0] a9_in,
  input  [31:0] a10_in,
  input  [31:0] a11_in,
  input  [11:0] b1_in,
  input  [11:0] b2_in,
  input  [11:0] b3_in,
  input  [11:0] b4_in,
  input  [11:0] b5_in,
  input  [11:0] b6_in,
  input  [11:0] b7_in,
  input  [11:0] b8_in,
  input  [11:0] b9_in,
  input  [11:0] b10_in,
  input  [11:0] b11_in,
  output [7:0] literal_data,
  output [1:0] literal_sel,
  output res_sel,
  output op,
  output [7:0] data,
  output data_wr,
  output [5:0] addr_in,
  output [5:0] addr_out,
  output [7:0] goto,
  output jump,
  output pc_enable,
  output skip
);

  wire and_1_out;
  wire [10:10] multiplexer_2_out;
  wire [11:0] B12;
  wire [31:0] A12;

  and and_1 (and_1_out, sel[0], sel[1], sel[2], sel[3], sel[4]);
  Multiplexer #(.select(5), .width(32), .enable("false")) multiplexer_1 (
    .in0(a1_in), .in1(a2_in), .in2(a3_in), .in3(a4_in), .in4(a5_in), .in5(a6_in), .in6(a7_in), .in7(a8_in),
    .in8(a9_in), .in9(a10_in), .in10(a11_in), .in11(A12), .in12({32{1'b0}}), .in13({32{1'b0}}),
    .in14({32{1'b0}}), .in15({32{1'b0}}), .in16({32{1'b0}}), .in17({32{1'b0}}), .in18({32{1'b0}}),
    .in19({32{1'b0}}), .in20({32{1'b0}}), .in21({32{1'b0}}), .in22({32{1'b0}}), .in23({32{1'b0}}),
    .in24({32{1'b0}}), .in25({32{1'b0}}), .in26({32{1'b0}}), .in27({32{1'b0}}), .in28({32{1'b0}}),
    .in29({32{1'b0}}), .in30({32{1'b0}}), .in31({32{1'b0}}),
    .out({addr_out[4:0], addr_in, data_wr, data, op, res_sel, literal_sel, literal_data}), .sel(sel));
  Multiplexer #(.select(5), .width(12), .enable("false")) multiplexer_2 (
    .in0(b1_in), .in1(b2_in), .in2(b3_in), .in3(b4_in), .in4(b5_in), .in5(b6_in), .in6(b7_in), .in7(b8_in),
    .in8(b9_in), .in9(b10_in), .in10(b11_in), .in11(B12), .in12({12{1'b0}}), .in13({12{1'b0}}),
    .in14({12{1'b0}}), .in15({12{1'b0}}), .in16({12{1'b0}}), .in17({12{1'b0}}), .in18({12{1'b0}}),
    .in19({12{1'b0}}), .in20({12{1'b0}}), .in21({12{1'b0}}), .in22({12{1'b0}}), .in23({12{1'b0}}),
    .in24({12{1'b0}}), .in25({12{1'b0}}), .in26({12{1'b0}}), .in27({12{1'b0}}), .in28({12{1'b0}}),
    .in29({12{1'b0}}), .in30({12{1'b0}}), .in31({12{1'b0}}),
    .out({skip, multiplexer_2_out[10], jump, goto, addr_out[5]}), .sel(sel));
  or or_1 (pc_enable, multiplexer_2_out[10], and_1_out);

  // Other names for the same wires on the sheet: A1[31:0] = a1_in; A2[31:0] = a2_in; A3[31:0] = a3_in;
  //   A4[31:0] = a4_in; A5[31:0] = a5_in; A6[31:0] = a6_in; A7[31:0] = a7_in; A8[31:0] = a8_in; A9[31:0] = a9_in;
  //   A10[31:0] = a10_in; A11[31:0] = a11_in; B1[11:0] = b1_in; B2[11:0] = b2_in; B3[11:0] = b3_in; B4[11:0] = b4_in;
  //   B5[11:0] = b5_in; B6[11:0] = b6_in; B7[11:0] = b7_in; B8[11:0] = b8_in; B9[11:0] = b9_in; B10[11:0] = b10_in;
  //   B11[11:0] = b11_in
endmodule

module barramento_test (
  input  [7:0] in_1,
  input  [1:0] in_2,
  input  in_3,
  input  in_4,
  input  [7:0] in_5,
  input  in_6,
  input  [5:0] in_7,
  input  [5:0] in_8,
  input  [7:0] in_9,
  input  in_10,
  input  in_11,
  input  in_12
);

  wire seletor_1_data_wr, seletor_1_jump, seletor_1_op, seletor_1_pc_enable, seletor_1_res_sel,
       seletor_1_skip;
  wire [1:0] seletor_1_literal_sel;
  wire [5:0] seletor_1_addr_in, seletor_1_addr_out;
  wire [7:0] seletor_1_data, seletor_1_goto, seletor_1_literal_data;
  wire [11:0] adapter_1_b;
  wire [31:0] adapter_1_a;

  adapter adapter_1 (
    .literal_data(in_1), .literal_sel(in_2), .res_sel(in_3), .op(in_4), .data(in_5), .data_wr(in_6),
    .addr_in(in_7), .addr_out(in_8), .goto(in_9), .jump(in_10), .pc_enable(in_11), .skip(in_12),
    .a(adapter_1_a), .b(adapter_1_b));
  seletor seletor_1 (
    .a1_in(adapter_1_a), .b1_in(adapter_1_b), .literal_data(seletor_1_literal_data),
    .literal_sel(seletor_1_literal_sel), .res_sel(seletor_1_res_sel), .op(seletor_1_op),
    .data(seletor_1_data), .data_wr(seletor_1_data_wr), .addr_in(seletor_1_addr_in),
    .addr_out(seletor_1_addr_out), .goto(seletor_1_goto), .jump(seletor_1_jump),
    .pc_enable(seletor_1_pc_enable), .skip(seletor_1_skip));  // open: sel, a2_in, a3_in, a4_in, a5_in, a6_in, a7_in, a8_in, a9_in, a10_in, a11_in, b2_in, b3_in, b4_in, b5_in, b6_in, b7_in, b8_in, b9_in, b10_in, b11_in
  // Probe on seletor_1_literal_data
  // Probe on seletor_1_literal_sel
  // Probe on seletor_1_res_sel
  // Probe on seletor_1_op
  // Probe on seletor_1_data
  // Probe on seletor_1_data_wr
  // Probe on seletor_1_addr_in
  // Probe on seletor_1_addr_out
  // Probe on seletor_1_goto
  // Probe on seletor_1_jump
  // Probe on seletor_1_pc_enable
  // Probe on seletor_1_skip
endmodule

module adapter (
  input  [7:0] literal_data,
  input  [1:0] literal_sel,
  input  res_sel,
  input  op,
  input  [7:0] data,
  input  data_wr,
  input  [5:0] addr_in,
  input  [5:0] addr_out,
  input  [7:0] goto,
  input  jump,
  input  pc_enable,
  input  skip,
  output [31:0] a,
  output [11:0] b
);


  assign a = {addr_out[4:0], addr_in, data_wr, data, op, res_sel, literal_sel, literal_data};
  assign b = {skip, pc_enable, jump, goto, addr_out[5]};
endmodule

module fun_goto (
  input  [12:0] opcode,
  output active,
  output [31:0] a,
  output [11:0] b
);

  and and_1 (active, opcode[12], ~opcode[11], opcode[10]);  // AND_Gate
  adapter adapter_1 (
    .literal_data({8{1'b0}}), .literal_sel(2'b00), .res_sel(1'b0), .op(1'b0), .data({8{1'b0}}),
    .data_wr(1'b0), .addr_in({6{1'b0}}), .addr_out({6{1'b0}}), .goto(opcode[7:0]), .jump(active),
    .pc_enable(1'b1), .skip(1'b0), .a(a), .b(b));
endmodule

module decode (
  input  p1,
  input  p2,
  input  p3,
  input  p4,
  input  p5,
  input  p6,
  input  p7,
  input  p8,
  input  p9,
  input  p10,
  input  p11,
  output [4:0] sel
);

  wire xor_1_out;
  wire [3:0] or_1_out;
  wire [4:0] multiplexer_1_out;

  or or_1 (or_1_out[0], p5, p1, p3, p7, p9, p11);
  or or_2 (or_1_out[1], p6, p2, p3, p7, p10, p11);
  or or_3 (or_1_out[2], p4, p5, p6, p7);
  or or_4 (or_1_out[3], p8, p9, p10, p11);
  ExactlyOne xor_1 (
    .out(xor_1_out), .in0(p1), .in1(p2), .in2(p3), .in3(p4), .in4(p5), .in5(p6), .in6(p7), .in7(p8),
    .in8(p9), .in9(p10), .in10(p11));
  Multiplexer #(.width(5), .enable("false")) multiplexer_1 (
    .in0({5{1'b0}}), .in1({1'b0, or_1_out}), .out(multiplexer_1_out), .sel(xor_1_out));
  Subtractor #(.width(5)) subtractor_1 (.a(multiplexer_1_out), .b(5'b00001), .out(sel));  // open: bin, bout
endmodule

module fun_movlw (
  input  [12:0] opcode,
  output active,
  output [31:0] a,
  output [11:0] b
);

  and and_1 (active, ~opcode[8], ~opcode[9], ~opcode[10], opcode[11], opcode[12]);  // AND_Gate
  adapter adapter_1 (
    .literal_data({8{1'b0}}), .literal_sel(2'b00), .res_sel(1'b0), .op(1'b0), .data(opcode[7:0]),
    .data_wr(opcode[12]), .addr_in({6{1'b1}}), .addr_out({6{1'b0}}), .goto({8{1'b0}}), .jump(1'b0),
    .pc_enable(1'b1), .skip(1'b0), .a(a), .b(b));
endmodule

module fun_movf (
  input  [12:0] opcode,
  output active,
  output [31:0] a,
  output [11:0] b
);

  wire [5:0] multiplexer_1_out;

  and and_1 (active, ~opcode[7], ~opcode[8], ~opcode[9], opcode[10], ~opcode[11], ~opcode[12]);  // AND_Gate
  Multiplexer #(.width(6), .enable("false")) multiplexer_1 (
    .in0({6{1'b1}}), .in1(opcode[5:0]), .out(multiplexer_1_out), .sel(opcode[6]));
  adapter adapter_1 (
    .literal_data({8{1'b0}}), .literal_sel(2'b10), .res_sel(active), .op(1'b0), .data({8{1'b0}}),
    .data_wr(active), .addr_in(multiplexer_1_out), .addr_out(opcode[5:0]), .goto({8{1'b0}}), .jump(1'b0),
    .pc_enable(active), .skip(1'b0), .a(a), .b(b));
endmodule

module fun_movwf (
  input  [12:0] opcode,
  input  [7:0] data_out,
  output active,
  output [31:0] a,
  output [11:0] b
);

  and and_1 (active, opcode[6], ~opcode[7], ~opcode[8], ~opcode[9], ~opcode[10], ~opcode[11], ~opcode[12]);  // AND_Gate
  adapter adapter_1 (
    .literal_data({8{1'b0}}), .literal_sel(2'b00), .res_sel(1'b0), .op(1'b0), .data(data_out),
    .data_wr(active), .addr_in(opcode[5:0]), .addr_out({6{1'b1}}), .goto({8{1'b0}}), .jump(1'b0),
    .pc_enable(active), .skip(1'b0), .a(a), .b(b));
endmodule

module fun_clrf (
  input  [12:0] opcode,
  output active,
  output [31:0] a,
  output [11:0] b
);

  and and_1 (active, opcode[6], opcode[7], ~opcode[8], ~opcode[9], ~opcode[10], ~opcode[11], ~opcode[12]);  // AND_Gate
  adapter adapter_1 (
    .literal_data({8{1'b0}}), .literal_sel(2'b00), .res_sel(1'b0), .op(1'b0), .data({8{1'b0}}),
    .data_wr(active), .addr_in(opcode[5:0]), .addr_out({6{1'b0}}), .goto({8{1'b0}}), .jump(1'b0),
    .pc_enable(active), .skip(1'b0), .a(a), .b(b));
endmodule

module fun_incf (
  input  [12:0] opcode,
  output active,
  output [31:0] a,
  output [11:0] b
);

  wire [5:0] multiplexer_1_out;

  and and_1 (active, ~opcode[7], opcode[8], ~opcode[9], opcode[10], ~opcode[11], ~opcode[12]);  // AND_Gate
  Multiplexer #(.width(6), .enable("false")) multiplexer_1 (
    .in0({6{1'b1}}), .in1(opcode[5:0]), .out(multiplexer_1_out), .sel(opcode[6]));
  adapter adapter_1 (
    .literal_data(8'h1), .literal_sel(2'b10), .res_sel(active), .op(1'b0), .data_wr(active),
    .addr_in(multiplexer_1_out), .addr_out(opcode[5:0]), .goto({8{1'b0}}), .jump(1'b0), .pc_enable(active),
    .skip(1'b0), .a(a), .b(b));  // open: data
endmodule

module fun_sublw (
  input  [12:0] opcode,
  output active,
  output [31:0] a,
  output [11:0] b
);

  and and_1 (active, ~opcode[8], opcode[9], opcode[10], opcode[11], opcode[12]);  // AND_Gate
  adapter adapter_1 (
    .literal_data(opcode[7:0]), .literal_sel(2'b10), .res_sel(active), .op(active), .data({8{1'b0}}),
    .data_wr(active), .addr_in({6{1'b1}}), .addr_out({6{1'b1}}), .goto({8{1'b0}}), .jump(1'b0),
    .pc_enable(active), .skip(1'b0), .a(a), .b(b));
endmodule

module fun_subwf (
  input  [12:0] opcode,
  output active,
  output [31:0] a,
  output [11:0] b,
  output [5:0] addr_out2
);

  wire [5:0] multiplexer_1_out;

  and and_1 (active, ~opcode[7], opcode[8], ~opcode[9], ~opcode[10], ~opcode[11], ~opcode[12]);  // AND_Gate
  Multiplexer #(.width(6), .enable("false")) multiplexer_1 (
    .in0({6{1'b1}}), .in1(opcode[5:0]), .out(multiplexer_1_out), .sel(opcode[6]));
  adapter adapter_1 (
    .literal_data({8{1'b0}}), .literal_sel(2'b11), .res_sel(active), .op(active), .data({8{1'b0}}),
    .data_wr(active), .addr_in(multiplexer_1_out), .addr_out({6{1'b1}}), .goto({8{1'b0}}), .jump(1'b0),
    .pc_enable(active), .skip(1'b0), .a(a), .b(b));

  assign addr_out2 = opcode[5:0];
endmodule

module fun_btfss (
  input  [12:0] opcode,
  input  [7:0] data_out,
  output active,
  output [31:0] a,
  output [11:0] b
);

  wire and_2_out, multiplexer_1_out;

  and and_1 (active, opcode[9], opcode[10], opcode[11], ~opcode[12]);  // AND_Gate
  Multiplexer #(.select(3), .enable("false")) multiplexer_1 (
    .in0(data_out[0]), .in1(data_out[1]), .in2(data_out[2]), .in3(data_out[3]), .in4(data_out[4]),
    .in5(data_out[5]), .in6(data_out[6]), .in7(data_out[7]), .out(multiplexer_1_out), .sel(opcode[8:6]));
  and and_2 (and_2_out, multiplexer_1_out, active);
  adapter adapter_1 (
    .literal_data({8{1'b0}}), .literal_sel(2'b00), .res_sel(1'b0), .op(1'b0), .data({8{1'b0}}),
    .data_wr(1'b0), .addr_in({6{1'b0}}), .addr_out(opcode[5:0]), .goto({8{1'b0}}), .jump(1'b0),
    .pc_enable(active), .skip(and_2_out), .a(a), .b(b));
endmodule

module fun_btfsc (
  input  [12:0] opcode,
  input  [7:0] data_out,
  output active,
  output [31:0] a,
  output [11:0] b
);

  wire and_2_out, multiplexer_1_out;

  and and_1 (active, ~opcode[9], opcode[10], opcode[11], ~opcode[12]);  // AND_Gate
  Multiplexer #(.select(3), .enable("false")) multiplexer_1 (
    .in0(data_out[0]), .in1(data_out[1]), .in2(data_out[2]), .in3(data_out[3]), .in4(data_out[4]),
    .in5(data_out[5]), .in6(data_out[6]), .in7(data_out[7]), .out(multiplexer_1_out), .sel(opcode[8:6]));
  and and_2 (and_2_out, ~multiplexer_1_out, active);  // AND_Gate
  adapter adapter_1 (
    .literal_data({8{1'b0}}), .literal_sel(2'b00), .res_sel(1'b0), .op(1'b0), .data({8{1'b0}}),
    .data_wr(1'b0), .addr_in({6{1'b0}}), .addr_out(opcode[5:0]), .goto({8{1'b0}}), .jump(1'b0),
    .pc_enable(active), .skip(and_2_out), .a(a), .b(b));
endmodule

module fun_addwf (
  input  [12:0] in_1,
  input  [7:0] in_2,
  output out_3,
  output [31:0] out_4,
  output [11:0] out_5
);

  wire and_2_out, multiplexer_1_out;

  and and_1 (out_3, ~in_1[9], in_1[10], in_1[11], ~in_1[12]);  // AND_Gate
  Multiplexer #(.select(3), .enable("false")) multiplexer_1 (
    .in0(in_2[0]), .in1(in_2[1]), .in2(in_2[2]), .in3(in_2[3]), .in4(in_2[4]), .in5(in_2[5]), .in6(in_2[6]),
    .in7(in_2[7]), .out(multiplexer_1_out), .sel(in_1[8:6]));
  and and_2 (and_2_out, ~multiplexer_1_out, out_3);  // AND_Gate
  adapter adapter_1 (
    .literal_data({8{1'b0}}), .literal_sel(2'b00), .res_sel(1'b0), .op(1'b0), .data({8{1'b0}}),
    .data_wr(1'b0), .addr_in({6{1'b0}}), .addr_out(in_1[5:0]), .goto({8{1'b0}}), .jump(1'b0),
    .pc_enable(out_3), .skip(and_2_out), .a(out_4), .b(out_5));
endmodule
