// Logisim project PICa0_5.circ as structural Verilog: 41 circuits, main circuit main
module main (
  input  rst
);

  wire clock_1_out, corestuff_1_gotoenable, corestuff_1_skip, corestuff_1_stall, pc_1_carrystall;
  wire [9:0] corestuff_1_pcadress, pc_1_out_8;
  wire [12:0] multiplexer_1_out, rom_1_data;

  Clock clock_1 (.out(clock_1_out));
  PC pc_1 (
    .reset(rst), .stall(corestuff_1_skip), .clock(clock_1_out), .addrGOTO(corestuff_1_pcadress),
    .goto(corestuff_1_gotoenable), .skipNext(corestuff_1_stall), .carryStall(pc_1_carrystall),
    .out_8(pc_1_out_8));
  coreStuff corestuff_1 (
    .opcode(multiplexer_1_out), .clock(clock_1_out), .reset(rst), .pcAdress(corestuff_1_pcadress),
    .gotoEnable(corestuff_1_gotoenable), .stall(corestuff_1_stall), .skip(corestuff_1_skip));
  ROM #(.addrWidth(10), .dataWidth(13)) rom_1 (.addr(pc_1_out_8), .data(rom_1_data));
  Multiplexer #(.width(13), .enable("false")) multiplexer_1 (
    .in0(rom_1_data), .in1({13{1'b0}}), .out(multiplexer_1_out), .sel(pc_1_carrystall));
endmodule

module reg4 (
  input  [7:0] wr_data,
  input  wr_enable,
  input  [5:0] wr_A,
  input  reset,
  input  clk,
  input  [5:0] r_A1,
  input  [5:0] r_A2,
  output [7:0] r_D1,
  output [7:0] r_D2
);

  wire demultiplexer_1_out0, demultiplexer_1_out1, demultiplexer_1_out2, demultiplexer_1_out3;
  wire [7:0] register_1_q, register_2_q, register_3_q, register_4_q;

  Demultiplexer #(.select(2), .enable("false")) demultiplexer_1 (
    .out0(demultiplexer_1_out0), .out1(demultiplexer_1_out1), .out2(demultiplexer_1_out2),
    .out3(demultiplexer_1_out3), .in(wr_enable), .sel(wr_A[1:0]));
  // Probe on r_A1[1:0]
  // Probe on r_A2[1:0]
  Register register_1 (.D(wr_data), .en(demultiplexer_1_out0), .clk(clk), .Q(register_1_q), .clr(reset));
  Register register_2 (.D(wr_data), .en(demultiplexer_1_out2), .clk(clk), .Q(register_2_q), .clr(reset));
  Register register_3 (.D(wr_data), .en(demultiplexer_1_out1), .clk(clk), .Q(register_3_q), .clr(reset));
  Register register_4 (.D(wr_data), .en(demultiplexer_1_out3), .clk(clk), .Q(register_4_q), .clr(reset));
  Multiplexer #(.select(2), .width(8), .enable("false")) multiplexer_1 (
    .in0(register_1_q), .in1(register_3_q), .in2(register_2_q), .in3(register_4_q), .out(r_D1),
    .sel(r_A1[1:0]));
  Multiplexer #(.select(2), .width(8), .enable("false")) multiplexer_2 (
    .in0(register_1_q), .in1(register_3_q), .in2(register_2_q), .in3(register_4_q), .out(r_D2),
    .sel(r_A2[1:0]));
endmodule

module reg16 (
  input  [7:0] wrData,
  input  wrEnable,
  input  [5:0] wrAdd,
  input  clk,
  input  reset,
  input  [5:0] RA,
  input  [5:0] ra2,
  output [7:0] rd1,
  output [7:0] rd2
);

  wire demultiplexer_1_out0, demultiplexer_1_out1, demultiplexer_1_out2, demultiplexer_1_out3;
  wire [7:0] reg4_1_r_d1, reg4_1_r_d2, reg4_2_r_d1, reg4_2_r_d2, reg4_3_r_d1, reg4_3_r_d2, reg4_4_r_d1,
       reg4_4_r_d2;

  Demultiplexer #(.select(2), .enable("false")) demultiplexer_1 (
    .out0(demultiplexer_1_out0), .out1(demultiplexer_1_out1), .out2(demultiplexer_1_out2),
    .out3(demultiplexer_1_out3), .in(wrEnable), .sel(wrAdd[3:2]));
  // Probe on RA[3:2]
  // Probe on ra2[3:2]
  reg4 reg4_1 (
    .r_D1(reg4_1_r_d1), .clk(clk), .wr_data(wrData), .wr_A(wrAdd), .r_A2(ra2), .r_A1(RA),
    .wr_enable(demultiplexer_1_out0), .r_D2(reg4_1_r_d2), .reset(reset));
  reg4 reg4_2 (
    .r_D1(reg4_2_r_d1), .clk(clk), .wr_data(wrData), .wr_A(wrAdd), .r_A2(ra2), .r_A1(RA),
    .wr_enable(demultiplexer_1_out1), .r_D2(reg4_2_r_d2), .reset(reset));
  reg4 reg4_3 (
    .r_D1(reg4_3_r_d1), .clk(clk), .wr_data(wrData), .wr_A(wrAdd), .r_A2(ra2), .r_A1(RA),
    .wr_enable(demultiplexer_1_out2), .r_D2(reg4_3_r_d2), .reset(reset));
  reg4 reg4_4 (
    .r_D1(reg4_4_r_d1), .clk(clk), .wr_data(wrData), .wr_A(wrAdd), .r_A2(ra2), .r_A1(RA),
    .wr_enable(demultiplexer_1_out3), .r_D2(reg4_4_r_d2), .reset(reset));
  Multiplexer #(.select(2), .width(8), .enable("false")) multiplexer_1 (
    .in0(reg4_1_r_d1), .in1(reg4_2_r_d1), .in2(reg4_3_r_d1), .in3(reg4_4_r_d1), .out(rd1), .sel(RA[3:2]));
  Multiplexer #(.select(2), .width(8), .enable("false")) multiplexer_2 (
    .in0(reg4_1_r_d2), .in1(reg4_2_r_d2), .in2(reg4_3_r_d2), .in3(reg4_4_r_d2), .out(rd2), .sel(ra2[3:2]));
endmodule

module reg64 (
  input  [7:0] wr_data,
  input  wr_enable,
  input  [5:0] wr_addres,
  input  clk,
  input  reset,
  input  [5:0] r_a1,
  input  [5:0] r_a2,
  output [7:0] r_data1,
  output [7:0] r_data2
);

  wire demultiplexer_1_out0, demultiplexer_1_out1, demultiplexer_1_out2, demultiplexer_1_out3;
  wire [7:0] reg16_1_rd1, reg16_1_rd2, reg16_2_rd1, reg16_2_rd2, reg16_3_rd1, reg16_3_rd2, reg16_4_rd1,
       reg16_4_rd2;

  Demultiplexer #(.select(2), .enable("false")) demultiplexer_1 (
    .out0(demultiplexer_1_out0), .out1(demultiplexer_1_out1), .out2(demultiplexer_1_out2),
    .out3(demultiplexer_1_out3), .in(wr_enable), .sel(wr_addres[5:4]));
  // Probe on r_a1[5:4]
  // Probe on r_a2[5:4]
  reg16 reg16_1 (
    .rd1(reg16_1_rd1), .clk(clk), .wrData(wr_data), .wrAdd(wr_addres), .ra2(r_a2), .RA(r_a1),
    .wrEnable(demultiplexer_1_out0), .rd2(reg16_1_rd2), .reset(reset));
  reg16 reg16_2 (
    .rd1(reg16_2_rd1), .clk(clk), .wrData(wr_data), .wrAdd(wr_addres), .ra2(r_a2), .RA(r_a1),
    .wrEnable(demultiplexer_1_out1), .rd2(reg16_2_rd2), .reset(reset));
  reg16 reg16_3 (
    .rd1(reg16_3_rd1), .clk(clk), .wrData(wr_data), .wrAdd(wr_addres), .ra2(r_a2), .RA(r_a1),
    .wrEnable(demultiplexer_1_out2), .rd2(reg16_3_rd2), .reset(reset));
  reg16 reg16_4 (
    .rd1(reg16_4_rd1), .clk(clk), .wrData(wr_data), .wrAdd(wr_addres), .ra2(r_a2), .RA(r_a1),
    .wrEnable(demultiplexer_1_out3), .rd2(reg16_4_rd2), .reset(reset));
  Multiplexer #(.select(2), .width(8), .enable("false")) multiplexer_1 (
    .in0(reg16_1_rd1), .in1(reg16_2_rd1), .in2(reg16_3_rd1), .in3(reg16_4_rd1), .out(r_data1), .sel(r_a1[5:4]));
  Multiplexer #(.select(2), .width(8), .enable("false")) multiplexer_2 (
    .in0(reg16_1_rd2), .in1(reg16_2_rd2), .in2(reg16_3_rd2), .in3(reg16_4_rd2), .out(r_data2), .sel(r_a2[5:4]));
endmodule

module usc (
  input  enable,
  input  clock,
  input  [12:0] opcode,
  output [5:0] command
);

  wire [5:0] multiplexer_1_out, multiplexer_2_out, multiplexer_3_out, multiplexer_4_out, multiplexer_5_out,
       multiplexer_6_out, multiplexer_7_out, multiplexer_8_out, multiplexer_9_out, multiplexer_10_out,
       multiplexer_11_out, multiplexer_12_out, multiplexer_13_out;

  Multiplexer #(.width(6), .enable("false")) multiplexer_1 (
    .in0(6'b001000), .in1(6'b001001), .out(multiplexer_1_out), .sel(opcode[7]));
  Multiplexer #(.select(4), .width(6), .enable("false")) multiplexer_2 (
    .in0(6'b110101), .in1(6'b110101), .in2(6'b110101), .in3(6'b000011), .in4(6'b000100), .in5(6'b110101),
    .in6(6'b110101), .in7(6'b110101), .in8(6'b110101), .in9(6'b110101), .in10(6'b110101), .in11(6'b110101),
    .in12(6'b110101), .in13(6'b110101), .in14(6'b110101), .in15(6'b110101), .out(multiplexer_2_out),
    .sel(opcode[3:0]));
  Multiplexer #(.select(4), .width(6), .enable("false")) multiplexer_3 (
    .in0(6'b100110), .in1(6'b100110), .in2(6'b100110), .in3(6'b100110), .in4(6'b100111), .in5(6'b100111),
    .in6(6'b100111), .in7(6'b100111), .in8(6'b101000), .in9(6'b101001), .in10(6'b110000), .in11(6'b110101),
    .in12(6'b110001), .in13(6'b110010), .in14(6'b110011), .in15(6'b110100), .out(multiplexer_3_out),
    .sel(opcode[11:8]));
  Multiplexer #(.width(6), .enable("false")) multiplexer_4 (
    .in0(6'b010110), .in1(6'b010111), .out(multiplexer_4_out), .sel(opcode[7]));
  Multiplexer #(.width(6), .enable("false")) multiplexer_5 (
    .in0(6'b011000), .in1(6'b011001), .out(multiplexer_5_out), .sel(opcode[7]));
  Multiplexer #(.width(6), .enable("false")) multiplexer_6 (
    .in0(6'b100000), .in1(6'b100001), .out(multiplexer_6_out), .sel(opcode[7]));
  Multiplexer #(.width(6), .enable("false")) multiplexer_7 (
    .in0(6'b010000), .in1(6'b010001), .out(multiplexer_7_out), .sel(opcode[7]));
  Multiplexer #(.width(6), .enable("false")) multiplexer_8 (
    .in0(6'b010010), .in1(6'b010011), .out(multiplexer_8_out), .sel(opcode[7]));
  Multiplexer #(.width(6), .enable("false")) multiplexer_9 (
    .in0(6'b010100), .in1(6'b010101), .out(multiplexer_9_out), .sel(opcode[7]));
  Multiplexer #(.select(4), .width(6), .enable("false")) multiplexer_10 (
    .in0(multiplexer_11_out), .in1(multiplexer_1_out), .in2(multiplexer_7_out), .in3(multiplexer_8_out),
    .in4(multiplexer_9_out), .in5(multiplexer_4_out), .in6(multiplexer_5_out), .in7(multiplexer_6_out),
    .in8(6'b100010), .in9(6'b100010), .in10(6'b100011), .in11(6'b100011), .in12(6'b100100), .in13(6'b100100),
    .in14(6'b100101), .in15(6'b100101), .out(multiplexer_10_out), .sel(opcode[11:8]));
  Multiplexer #(.select(4), .width(6), .enable("false")) multiplexer_11 (
    .in0(multiplexer_12_out), .in1(6'b110101), .in2(multiplexer_2_out), .in3(6'b110101), .in4(6'b000101),
    .in5(6'b000101), .in6(6'b000101), .in7(6'b000101), .in8(6'b000110), .in9(6'b000110), .in10(6'b000110),
    .in11(6'b000110), .in12(6'b000111), .in13(6'b000111), .in14(6'b000111), .in15(6'b000111),
    .out(multiplexer_11_out), .sel(opcode[7:4]));
  Multiplexer #(.select(4), .width(6), .enable("false")) multiplexer_12 (
    .in0({6{1'b0}}), .in1(6'b110101), .in2(6'b110101), .in3(6'b110101), .in4(6'b000001), .in5(6'b000010),
    .in6(6'b110101), .in7(6'b110101), .in8(6'b110101), .in9(6'b110101), .in10(6'b110101), .in11(6'b110101),
    .in12(6'b110101), .in13(6'b110101), .in14(6'b110101), .in15(6'b110101), .out(multiplexer_12_out),
    .sel(opcode[3:0]));
  Multiplexer #(.width(6), .enable("false")) multiplexer_13 (
    .in0(multiplexer_10_out), .in1(multiplexer_3_out), .out(multiplexer_13_out), .sel(opcode[12]));
  Register #(.width(6)) register_1 (.D(multiplexer_13_out), .en(enable), .clk(clock), .Q(command));  // open: clr
endmodule

module triStateMachine (
  input  reset,
  input  clock,
  input  nextState,
  output [1:0] stateNumber
);

  Counter #(.width(2), .max('h3)) counter_1 (
    .clr(reset), .up(1'b1), .count(nextState), .clk(clock), .Q(stateNumber));  // open: load, D, carry
endmodule

module PC (
  input  reset,
  input  stall,
  input  clock,
  input  [9:0] addrGOTO,
  input  goto,
  input  skipNext,
  output carryStall,
  output [9:0] out_8
);

  wire not_1_out, or_1_out;
  wire [9:0] adder_1_out, multiplexer_1_out;

  Adder #(.width(10)) adder_1 (.a(10'h2), .b(out_8), .out(adder_1_out));  // open: cin, cout
  not not_1 (not_1_out, stall);
  Multiplexer #(.width(10), .enable("false")) multiplexer_1 (
    .in0(addrGOTO), .in1(adder_1_out), .out(multiplexer_1_out), .sel(skipNext));
  or or_1 (or_1_out, goto, skipNext);
  Counter #(.width(10), .max('h3ff), .ongoal("stay"), .trigger("falling")) counter_1 (
    .clr(reset), .load(or_1_out), .up(1'b1), .count(not_1_out), .clk(clock), .D(multiplexer_1_out), .Q(out_8));  // open: carry

  assign carryStall = stall;
endmodule

module coreStuff (
  input  [12:0] opcode,
  input  clock,
  input  reset,
  output [9:0] pcAdress,
  output gotoEnable,
  output stall,
  output skip
);

  wire and_2_out, and_3_out, bitselector_1_out, bitselector_2_out, comparator_1_eq, comparator_2_eq,
       comparator_3_eq, movf14_1_renable, movf14_1_wenable, multiplexer_7_out, multiplexer_8_out,
       multiplexer_9_out, multiplexer_10_out, multiplexer_12_out, multiplexer_13_out, not_1_out, not_2_out,
       not_3_out, subwf8_1_renable, subwf8_1_wenable;
  wire [5:0] multiplexer_3_out, multiplexer_4_out, multiplexer_6_out, usc_1_command;
  wire [7:0] adder_2_out, bcf22_1_data, dataFromW, dataREG, dataToStuffInREG, inc, movf14_1_data,
       multiplexer_1_out, multiplexer_2_out, multiplexer_5_out, multiplexer_14_out, multiplexer_15_out,
       subtractor_1_out, subwf8_1_data;

  not not_1 (not_1_out, reset);
  usc usc_1 (.enable(not_1_out), .clock(clock), .opcode(opcode), .command(usc_1_command));
  Subtractor subtractor_1 (.a(opcode[7:0]), .b(dataFromW), .out(subtractor_1_out));  // open: bin, bout
  Adder adder_1 (.a(dataFromW), .b(8'h1), .out(inc));  // open: cin, cout
  Adder adder_2 (.a(opcode[7:0]), .b(dataFromW), .out(adder_2_out));  // open: cin, cout
  Register #(.trigger("falling")) workReg (
    .D(multiplexer_5_out), .en(multiplexer_10_out), .clk(clock), .Q(dataFromW), .clr(reset));
  reg64 reg64_1 (
    .wr_data(dataToStuffInREG), .wr_enable(multiplexer_9_out), .wr_addres(multiplexer_6_out), .clk(clock),
    .reset(reset), .r_a1(multiplexer_6_out), .r_data1(dataREG));  // open: r_a2, r_data2
  Multiplexer #(.select(5), .width(8), .enable("false")) multiplexer_1 (
    .in6({8{1'b0}}), .in8(subwf8_1_data), .in14(movf14_1_data), .in16(inc), .in28(opcode[7:0]),
    .out(multiplexer_1_out), .sel(usc_1_command[4:0]));  // open: in0, in1, in2, in3, in4, in5, in7, in9, in10, in11, in12, in13, in15, in17, in18, in19, in20, in21, in22, in23, in24, in25, in26, in27, in29, in30, in31
  Multiplexer #(.select(5), .width(8), .enable("false")) multiplexer_2 (
    .in1(subtractor_1_out), .in2(adder_2_out), .in4({8{1'b0}}), .in5({8{1'b0}}), .in6({8{1'b0}}),
    .in7({8{1'b0}}), .in8({8{1'b0}}), .in9({8{1'b0}}), .in10({8{1'b0}}), .in11({8{1'b0}}), .in12({8{1'b0}}),
    .in13({8{1'b0}}), .in14({8{1'b0}}), .in15({8{1'b0}}), .in16({8{1'b0}}), .in17({8{1'b0}}),
    .in18({8{1'b0}}), .in19({8{1'b0}}), .in20({8{1'b0}}), .in21({8{1'b0}}), .in22({8{1'b0}}),
    .in23({8{1'b0}}), .in24({8{1'b0}}), .in25({8{1'b0}}), .in26({8{1'b0}}), .in27({8{1'b0}}),
    .in28({8{1'b0}}), .in29({8{1'b0}}), .in30({8{1'b0}}), .in31({8{1'b0}}), .out(multiplexer_2_out),
    .sel(usc_1_command[4:0]));  // open: in0, in3
  Multiplexer #(.select(5), .width(6), .enable("false")) multiplexer_3 (
    .in5(opcode[5:0]), .in7(opcode[5:0]), .in8(opcode[5:0]), .in14(opcode[5:0]), .in16(opcode[5:0]),
    .in22(opcode[5:0]), .in23(opcode[5:0]), .in24(opcode[5:0]), .in25(opcode[5:0]), .out(multiplexer_3_out),
    .sel(usc_1_command[4:0]));  // open: in0, in1, in2, in3, in4, in6, in9, in10, in11, in12, in13, in15, in17, in18, in19, in20, in21, in26, in27, in28, in29, in30, in31
  Multiplexer #(.select(5), .width(6), .enable("false")) multiplexer_4 (
    .in2({6{1'b0}}), .in4({6{1'b0}}), .in5({6{1'b0}}), .in6({6{1'b0}}), .in7({6{1'b0}}), .in8({6{1'b0}}),
    .in9({6{1'b0}}), .in10({6{1'b0}}), .in11({6{1'b0}}), .in12({6{1'b0}}), .in13({6{1'b0}}),
    .in14({6{1'b0}}), .in15({6{1'b0}}), .in16({6{1'b0}}), .in17({6{1'b0}}), .in18({6{1'b0}}),
    .in19({6{1'b0}}), .in20({6{1'b0}}), .in21({6{1'b0}}), .in22({6{1'b0}}), .in23({6{1'b0}}),
    .in24({6{1'b0}}), .in25({6{1'b0}}), .in26({6{1'b0}}), .in27({6{1'b0}}), .in28({6{1'b0}}),
    .in29({6{1'b0}}), .in30({6{1'b0}}), .in31({6{1'b0}}), .out(multiplexer_4_out), .sel(usc_1_command[4:0]));  // open: in0, in1, in3
  Multiplexer #(.width(8), .enable("false")) multiplexer_5 (
    .in0(multiplexer_1_out), .in1(multiplexer_2_out), .out(multiplexer_5_out), .sel(usc_1_command[5]));
  Multiplexer #(.width(6), .enable("false")) multiplexer_6 (
    .in0(multiplexer_3_out), .in1(multiplexer_4_out), .out(multiplexer_6_out), .sel(usc_1_command[5]));
  Multiplexer #(.select(5), .enable("false")) multiplexer_7 (
    .in0(1'b0), .in5(1'b0), .in6(1'b1), .in8(subwf8_1_wenable), .in14(movf14_1_wenable), .in16(not_2_out),
    .in28(1'b1), .out(multiplexer_7_out), .sel(usc_1_command[4:0]));  // open: in1, in2, in3, in4, in7, in9, in10, in11, in12, in13, in15, in17, in18, in19, in20, in21, in22, in23, in24, in25, in26, in27, in29, in30, in31
  Multiplexer #(.select(5), .enable("false")) multiplexer_8 (
    .in0(1'b0), .in1(1'b0), .in5(1'b1), .in6(1'b0), .in7(1'b1), .in8(subwf8_1_renable),
    .in14(movf14_1_renable), .in16(opcode[6]), .in22(1'b1), .in23(1'b1), .in25(1'b0), .in28(1'b0),
    .out(multiplexer_8_out), .sel(usc_1_command[4:0]));  // open: in2, in3, in4, in9, in10, in11, in12, in13, in15, in17, in18, in19, in20, in21, in24, in26, in27, in29, in30, in31
  not not_2 (not_2_out, opcode[6]);
  MOVF14 movf14_1 (
    .opcode(opcode), .rData(dataREG), .wEnable(movf14_1_wenable), .rEnable(movf14_1_renable),
    .data(movf14_1_data));  // open: wData, addres
  Multiplexer #(.enable("false")) multiplexer_9 (
    .in0(multiplexer_8_out), .in1(multiplexer_13_out), .out(multiplexer_9_out), .sel(usc_1_command[5]));
  Multiplexer #(.enable("false")) multiplexer_10 (
    .in0(multiplexer_7_out), .in1(multiplexer_12_out), .out(multiplexer_10_out), .sel(usc_1_command[5]));
  SUBWF8 subwf8_1 (
    .opcode(opcode), .wData(dataFromW), .rData(dataREG), .wEnable(subwf8_1_wenable),
    .rEnable(subwf8_1_renable), .data(subwf8_1_data));  // open: addres
  BitSelector bitselector_1 (.in(dataREG), .out(bitselector_1_out), .sel(opcode[8:6]));
  BitSelector bitselector_2 (.in(dataREG), .out(bitselector_2_out), .sel(opcode[8:6]));
  Comparator #(.width(6), .mode("unsigned")) comparator_1 (
    .a(usc_1_command), .b(6'b100011), .eq(comparator_1_eq));  // open: gt, lt
  and and_1 (gotoEnable, usc_1_command[0], usc_1_command[1], ~usc_1_command[2], usc_1_command[3], usc_1_command[4], ~usc_1_command[5]);  // AND_Gate
  Multiplexer #(.width(10), .enable("false")) multiplexer_11 (.in1(opcode[9:0]), .sel(gotoEnable));  // open: in0, out
  Multiplexer #(.select(5), .enable("false")) multiplexer_12 (
    .in1(1'b1), .in2(1'b1), .in4(1'b0), .in5(1'b0), .in6(1'b0), .in7(1'b0), .in8(1'b0), .in9(1'b0),
    .in10(1'b0), .in11(1'b0), .in12(1'b0), .in13(1'b0), .in14(1'b0), .in15(1'b0), .in16(1'b0), .in17(1'b0),
    .in18(1'b0), .in19(1'b0), .in20(1'b0), .in21(1'b0), .in22(1'b0), .in23(1'b0), .in24(1'b0), .in25(1'b0),
    .in26(1'b0), .in27(1'b0), .in28(1'b0), .in29(1'b0), .in30(1'b0), .in31(1'b0), .out(multiplexer_12_out),
    .sel(usc_1_command[4:0]));  // open: in0, in3
  not not_3 (not_3_out, bitselector_2_out);
  Multiplexer #(.select(5), .enable("false")) multiplexer_13 (
    .in1(1'b0), .in2(1'b0), .in4(1'b0), .in5(1'b0), .in6(1'b0), .in7(1'b0), .in8(1'b0), .in9(1'b0),
    .in10(1'b0), .in11(1'b0), .in12(1'b0), .in13(1'b0), .in14(1'b0), .in15(1'b0), .in16(1'b0), .in17(1'b0),
    .in18(1'b0), .in19(1'b0), .in20(1'b0), .in21(1'b0), .in22(1'b0), .in23(1'b0), .in24(1'b0), .in25(1'b0),
    .in26(1'b0), .in27(1'b0), .in28(1'b0), .in29(1'b0), .in30(1'b0), .in31(1'b0), .out(multiplexer_13_out),
    .sel(usc_1_command[4:0]));  // open: in0, in3
  Comparator #(.width(6), .mode("unsigned")) comparator_2 (
    .a(usc_1_command), .b(6'b100101), .eq(comparator_2_eq));  // open: gt, lt
  Comparator #(.width(6), .mode("unsigned")) comparator_3 (
    .a(usc_1_command), .b(6'b100100), .eq(comparator_3_eq));  // open: gt, lt
  BCF22 bcf22_1 (.upOrDown(comparator_1_eq), .rData(dataREG), .bitSelector(opcode[8:6]), .data(bcf22_1_data));
  and and_2 (and_2_out, comparator_2_eq, bitselector_1_out);
  or or_1 (skip, and_2_out, and_3_out);
  and and_3 (and_3_out, not_3_out, comparator_3_eq);
  Multiplexer #(.select(5), .width(8), .enable("false")) multiplexer_14 (
    .in5(opcode[7:0]), .in7({8{1'b0}}), .in8(subwf8_1_data), .in14(movf14_1_data), .in16(inc),
    .in22(bcf22_1_data), .in23(bcf22_1_data), .out(multiplexer_14_out), .sel(usc_1_command[4:0]));  // open: in0, in1, in2, in3, in4, in6, in9, in10, in11, in12, in13, in15, in17, in18, in19, in20, in21, in24, in25, in26, in27, in28, in29, in30, in31
  Multiplexer #(.select(5), .width(8), .enable("false")) multiplexer_15 (
    .in4({8{1'b0}}), .in5({8{1'b0}}), .in6({8{1'b0}}), .in7({8{1'b0}}), .in8({8{1'b0}}), .in9({8{1'b0}}),
    .in10({8{1'b0}}), .in11({8{1'b0}}), .in12({8{1'b0}}), .in13({8{1'b0}}), .in14({8{1'b0}}),
    .in15({8{1'b0}}), .in16({8{1'b0}}), .in17({8{1'b0}}), .in18({8{1'b0}}), .in19({8{1'b0}}),
    .in20({8{1'b0}}), .in21({8{1'b0}}), .in22({8{1'b0}}), .in23({8{1'b0}}), .in24({8{1'b0}}),
    .in25({8{1'b0}}), .in26({8{1'b0}}), .in27({8{1'b0}}), .in28({8{1'b0}}), .in29({8{1'b0}}),
    .in30({8{1'b0}}), .in31({8{1'b0}}), .out(multiplexer_15_out), .sel(usc_1_command[4:0]));  // open: in0, in1, in2, in3
  Multiplexer #(.width(8), .enable("false")) multiplexer_16 (
    .in0(multiplexer_14_out), .in1(multiplexer_15_out), .out(dataToStuffInREG), .sel(usc_1_command[5]));

  assign pcAdress = opcode[9:0];

  // Other names for the same wires on the sheet: addrFromOPT[5:0] = opcode[5:0]; cteFromOPT[7:0] = opcode[7:0];
  //   selector = opcode[6]

  // Notes on the sheet:
  //   data
  //   0
  //   addres to stuff in reg
  //   0
  //   addres
  //   Data to opToW
  //   enable wr on reg Work
  //   enable wr on reg bank
  //   0
  //   data to stuff in reg
endmodule

module ADDWF13 (
  input  [12:0] opcode,
  input  [7:0] wData,
  input  [7:0] rData,
  output wEnable,
  output rEnable,
  output [7:0] data,
  output [5:0] addres
);
endmodule

module ANDLW29 (
  input  [12:0] opcode,
  input  [7:0] wData,
  input  [7:0] rData,
  output wEnable,
  output rEnable,
  output [7:0] data,
  output [5:0] addres
);
endmodule

module ANDWF11 (
  input  [12:0] opcode,
  input  [7:0] wData,
  input  [7:0] rData,
  output wEnable,
  output rEnable,
  output [7:0] data,
  output [5:0] addres
);
endmodule

module BCF22 (
  input  upOrDown,
  input  [7:0] rData,
  input  [2:0] bitSelector,
  output [7:0] data
);

  Multiplexer #(.select(3), .width(8), .enable("false")) multiplexer_1 (
    .in0({rData[7:1], upOrDown}), .in1({rData[7:2], upOrDown, rData[0]}),
    .in2({rData[7:3], upOrDown, rData[1:0]}), .in3({rData[7:4], upOrDown, rData[2:0]}),
    .in4({rData[7:5], upOrDown, rData[3:0]}), .in5({rData[7:6], upOrDown, rData[4:0]}),
    .in6({rData[7], upOrDown, rData[5:0]}), .in7({upOrDown, rData[6:0]}), .out(data), .sel(bitSelector));
endmodule

module BSF23 (
  input  [12:0] opcode,
  input  [7:0] wData,
  input  [7:0] rData,
  output wEnable,
  output rEnable,
  output [7:0] data,
  output [5:0] addres
);
endmodule

module BTFSS25 (
  input  [12:0] opcode,
  input  [7:0] wData,
  input  [7:0] rData,
  output wEnable,
  output rEnable,
  output [7:0] data,
  output [5:0] addres
);
endmodule

module BTFSC24 (
  input  [12:0] opcode,
  input  [7:0] wData,
  input  [7:0] rData,
  output wEnable,
  output rEnable,
  output [7:0] data,
  output [5:0] addres
);
endmodule

module CALL26 (
  input  [12:0] opcode,
  input  [7:0] wData,
  input  [7:0] rData,
  output wEnable,
  output rEnable,
  output [7:0] data,
  output [5:0] addres
);
endmodule

module CLRF7 (
  input  [12:0] opcode,
  input  [7:0] wData,
  input  [7:0] rData,
  output wEnable,
  output rEnable,
  output [7:0] data,
  output [5:0] addres
);
endmodule

module CLRW6 (
  input  [12:0] opcode,
  input  [7:0] wData,
  input  [7:0] rData,
  output wEnable,
  output rEnable,
  output [7:0] data,
  output [5:0] addres
);
endmodule

module CLRWDT4 (
  input  [12:0] opcode,
  input  [7:0] wData,
  input  [7:0] rData,
  output wEnable,
  output rEnable,
  output [7:0] data,
  output [5:0] addres
);
endmodule

module COMF15 (
  input  [12:0] opcode,
  input  [7:0] wData,
  input  [7:0] rData,
  output wEnable,
  output rEnable,
  output [7:0] data,
  output [5:0] addres
);
endmodule

module DECF9 (
  input  [12:0] opcode,
  input  [7:0] wData,
  input  [7:0] rData,
  output wEnable,
  output rEnable,
  output [7:0] data,
  output [5:0] addres
);
endmodule

module DECFSZ17 (
  input  [12:0] opcode,
  input  [7:0] wData,
  input  [7:0] rData,
  output wEnable,
  output rEnable,
  output [7:0] data,
  output [5:0] addres
);
endmodule

module GOTO27 (
  input  [12:0] opcode,
  output [9:0] pcAddres,
  output GOtoGOTO,
  output wEnable,
  output rEnable,
  output [7:0] data,
  output [5:0] addres
);

  and and_1 (GOtoGOTO, opcode[10], ~opcode[11], opcode[12]);  // AND_Gate

  assign pcAddres = opcode[9:0];
endmodule

module INCF16 (
  input  [12:0] opcode,
  input  [7:0] wData,
  input  [7:0] rData,
  output wEnable,
  output rEnable,
  output [7:0] data,
  output [5:0] addres
);
endmodule

module INCFSZ21 (
  input  [12:0] opcode,
  input  [7:0] wData,
  input  [7:0] rData,
  output wEnable,
  output rEnable,
  output [7:0] data,
  output [5:0] addres
);
endmodule

module IORLW31 (
  input  [12:0] opcode,
  input  [7:0] wData,
  input  [7:0] rData,
  output wEnable,
  output rEnable,
  output [7:0] data,
  output [5:0] addres
);
endmodule

module MOVF14 (
  input  [12:0] opcode,
  input  [7:0] wData,
  input  [7:0] rData,
  output wEnable,
  output rEnable,
  output [7:0] data,
  output [5:0] addres
);

  not not_1 (wEnable, opcode[6]);

  assign addres = opcode[5:0];
  assign data = rData;
  assign rEnable = opcode[6];
endmodule

module MOVLW28 (
  input  [12:0] opcode,
  input  [7:0] wData,
  input  [7:0] rData,
  output wEnable,
  output rEnable,
  output [7:0] data,
  output [5:0] addres
);
endmodule

module MOVWF5 (
  input  [12:0] opcode,
  input  [7:0] wData,
  input  [7:0] rData,
  output wEnable,
  output rEnable,
  output [7:0] data,
  output [5:0] addres
);
endmodule

module nop0 (
  input  [12:0] opcode,
  input  [7:0] wData,
  input  [7:0] rData,
  output wEnable,
  output rEnable,
  output [7:0] data,
  output [5:0] addres
);
endmodule

module RETFIE2 (
  input  [12:0] opcode,
  input  [7:0] wData,
  input  [7:0] rData,
  output wEnable,
  output rEnable,
  output [7:0] data,
  output [5:0] addres
);
endmodule

module RETLW30 (
  input  [12:0] opcode,
  input  [7:0] wData,
  input  [7:0] rData,
  output wEnable,
  output rEnable,
  output [7:0] data,
  output [5:0] addres
);
endmodule

module RETURN1 (
  input  [12:0] opcode,
  input  [7:0] wData,
  input  [7:0] rData,
  output wEnable,
  output rEnable,
  output [7:0] data,
  output [5:0] addres
);
endmodule

module RLF19 (
  input  [12:0] opcode,
  input  [7:0] wData,
  input  [7:0] rData,
  output wEnable,
  output rEnable,
  output [7:0] data,
  output [5:0] addres
);
endmodule

module RRF18 (
  input  [12:0] opcode,
  input  [7:0] wData,
  input  [7:0] rData,
  output wEnable,
  output rEnable,
  output [7:0] data,
  output [5:0] addres
);
endmodule

module SLEEP3 (
  input  [12:0] opcode,
  input  [7:0] wData,
  input  [7:0] rData,
  output wEnable,
  output rEnable,
  output [7:0] data,
  output [5:0] addres
);
endmodule

module SUBLW33 (
  input  [12:0] opcode,
  input  [7:0] wData,
  input  [7:0] rData,
  output wEnable,
  output rEnable,
  output [7:0] data,
  output [5:0] addres
);
endmodule

module SUBWF8 (
  input  [12:0] opcode,
  input  [7:0] wData,
  input  [7:0] rData,
  output wEnable,
  output rEnable,
  output [7:0] data,
  output [5:0] addres
);

  Subtractor subtractor_1 (.a(rData), .b(wData), .out(data));  // open: bin, bout
  not not_1 (wEnable, opcode[6]);

  assign rEnable = opcode[6];
endmodule

module SWAPF20 (
  input  [12:0] opcode,
  input  [7:0] wData,
  input  [7:0] rData,
  output wEnable,
  output rEnable,
  output [7:0] data,
  output [5:0] addres
);
endmodule

module XORLW32 (
  input  [12:0] opcode,
  input  [7:0] wData,
  input  [7:0] rData,
  output wEnable,
  output rEnable,
  output [7:0] data,
  output [5:0] addres
);
endmodule

module XORWF12 (
  input  [12:0] opcode,
  input  [7:0] wData,
  input  [7:0] rData,
  output wEnable,
  output rEnable,
  output [7:0] data,
  output [5:0] addres
);
endmodule
